// Logisim project Group_1_digital_lock_final.circ as structural Verilog: 28 circuits, main circuit main
module main (
);

  wire _0_out, _1_out, _2_out, _3_out, _4_out, _5_out, _6_out, _7_out, _8_out, _9_out, Admin_out,
       button_2_out, button_3_out, button_out, Edit_out, On_Off_out, pattern_lock_1_a, pattern_lock_1_a_2,
       pattern_lock_1_a_3, pattern_lock_1_b, pattern_lock_1_b_2, pattern_lock_1_b_3, pattern_lock_1_c,
       pattern_lock_1_c_2, pattern_lock_1_c_3, pattern_lock_1_d, pattern_lock_1_d_2, pattern_lock_1_d_3,
       pattern_lock_1_dot, pattern_lock_1_dot_2, pattern_lock_1_dot_3, pattern_lock_1_e, pattern_lock_1_e_2,
       pattern_lock_1_e_3, pattern_lock_1_f, pattern_lock_1_f_2, pattern_lock_1_f_3, pattern_lock_1_g,
       pattern_lock_1_g_2, pattern_lock_1_g_3, View_out;

  Button _1 (.out(_1_out));
  Button _4 (.out(_4_out));
  Button _7 (.out(_7_out));
  Button button (.out(button_out));
  Button Admin (.out(Admin_out));
  Button View (.out(View_out));
  Button _2 (.out(_2_out));
  Button _5 (.out(_5_out));
  Button _8 (.out(_8_out));
  Button _0 (.out(_0_out));
  Button Edit (.out(Edit_out));
  Button _3 (.out(_3_out));
  Button _6 (.out(_6_out));
  Button _9 (.out(_9_out));
  Button button_2 (.out(button_2_out));
  Button button_3 (.out(button_3_out));
  Button On_Off (.out(On_Off_out));
  Pattern_lock pattern_lock_1 (
    .D0(_0_out), .D1(_1_out), .D2(_2_out), .D3(_3_out), .D4(_4_out), .D5(_5_out), .D6(_6_out), .D7(_7_out),
    .D8(_8_out), .D9(_9_out), .mode(button_2_out), .reset(button_out), .Admin(Admin_out), .View(View_out),
    .Edit(Edit_out), .Next(button_3_out), .in_2(On_Off_out), .A(pattern_lock_1_a), .B(pattern_lock_1_b),
    .C(pattern_lock_1_c), .D(pattern_lock_1_d), .E(pattern_lock_1_e), .F(pattern_lock_1_f),
    .G(pattern_lock_1_g), .Dot(pattern_lock_1_dot), .B_2(pattern_lock_1_b_2), .A_2(pattern_lock_1_a_2),
    .F_2(pattern_lock_1_f_2), .G_2(pattern_lock_1_g_2), .E_2(pattern_lock_1_e_2), .D_2(pattern_lock_1_d_2),
    .C_2(pattern_lock_1_c_2), .Dot_2(pattern_lock_1_dot_2), .A_3(pattern_lock_1_a_3),
    .B_3(pattern_lock_1_b_3), .C_3(pattern_lock_1_c_3), .D_3(pattern_lock_1_d_3), .E_3(pattern_lock_1_e_3),
    .F_3(pattern_lock_1_f_3), .G_3(pattern_lock_1_g_3), .Dot_3(pattern_lock_1_dot_3));
  _7_Segment_Display u_7_segment_display_1 (
    .g(pattern_lock_1_g), .f(pattern_lock_1_f), .a(pattern_lock_1_a), .b(pattern_lock_1_b),
    .e(pattern_lock_1_e), .d(pattern_lock_1_d), .c(pattern_lock_1_c), .dp(pattern_lock_1_dot));
  _7_Segment_Display u_7_segment_display_2 (
    .g(pattern_lock_1_g_3), .f(pattern_lock_1_f_3), .a(pattern_lock_1_a_3), .b(pattern_lock_1_b_3),
    .e(pattern_lock_1_e_3), .d(pattern_lock_1_d_3), .c(pattern_lock_1_c_3), .dp(pattern_lock_1_dot_3));
  _7_Segment_Display u_7_segment_display_3 (
    .g(pattern_lock_1_g_2), .f(pattern_lock_1_f_2), .a(pattern_lock_1_a_2), .b(pattern_lock_1_b_2),
    .e(pattern_lock_1_e_2), .d(pattern_lock_1_d_2), .c(pattern_lock_1_c_2), .dp(pattern_lock_1_dot_2));

  // Notes on the sheet:
  //   Digit display
  //   Lock status/Mode
  //   Admin display
  //   1. Press admin
  //   1. Press View
  //   2. Enter new digit
  //   3. Press Edit again
  //   Press * to lock/reset the lock
  //   To enter admin mode:
  //   2. Press 000000 as admin password
  //   To view passwords (admin mode only):
  //   2. Press  > to go to next digit
  //   To Edit 1 digit (admin mode only):
  //   1. Press Edit when you reach the pin
  //   To exit admin mode, press admin again
  //   L=Locked
  //   U=Unlocked
  //   I=Invalid password
  //   S=Saved
  //   A=Admin mode
  //   Enable tick simulation to allow auto reset
  //   Press On/Off to turn on.
  //   Stored Pins: 210420, 222222,123451
  //   Press # to add new password (only in user mode)
  //   C=changing
endmodule

// Decimal to Exces 3
module Decimal_to_Excess_3 (
  input  On_Off,
  input  D0,
  input  D1,
  input  D2,
  input  D3,
  input  D4,
  input  D5,
  input  D6,
  input  D7,
  input  D8,
  input  D9,
  input  mode,
  input  reset,
  input  admin,
  input  View,
  input  in_16,
  input  in_17,
  output Constant_enable,
  output Enable,
  output B0,
  output B1,
  output B2,
  output B3,
  output Mode_2,
  output Key,
  output Reset_2,
  output admin_2,
  output view_2,
  output edit,
  output out_30,
  output out_31
);

  wire and_7_out, buffer_1_out_3, or_1_out, or_2_out, or_3_out, or_4_out, or_5_out, or_7_out;

  or or_1 (or_1_out, D0, D2, D4, D6, D8);
  or or_2 (or_2_out, D0, D3, D4, D7, D8);
  or or_3 (or_3_out, D1, D2, D3, D4, D9);
  or or_4 (or_4_out, D5, D6, D7, D8, D9);
  or or_5 (or_5_out, D0, D1, D2, D3, D4, D5, D6, D7, D8, D9);
  T_Flip_Flop t_ff_1 (.clk(On_Off), .T(On_Off), .Q(Constant_enable));  // open: Qn, preset, reset, en
  and and_1 (B0, Constant_enable, or_1_out);
  and and_2 (B1, Constant_enable, or_2_out);
  and and_3 (B2, Constant_enable, or_3_out);
  and and_4 (B3, Constant_enable, or_4_out);
  and and_5 (Mode_2, Constant_enable, mode);
  and and_6 (Key, Constant_enable, or_5_out);
  and and_7 (and_7_out, Constant_enable, reset);
  and and_8 (admin_2, Constant_enable, admin);
  and and_9 (view_2, Constant_enable, View);
  buf and_10 (edit, Constant_enable);  // AND_Gate
  and and_11 (out_30, Constant_enable, in_16);
  and and_12 (out_31, Constant_enable, in_17);
  or or_6 (Reset_2, and_7_out, buffer_1_out_3);
  or or_7 (or_7_out, Constant_enable, admin_2);
  Buffer buffer_1 (.in_1(or_7_out), .in_2(Key), .out_3(buffer_1_out_3));

  assign Enable = On_Off;
endmodule

module Comparator (
  input  C0,
  input  C1,
  input  C2,
  input  C3,
  input  S0,
  input  S1,
  input  S2,
  input  S3,
  output out_9
);

  wire xnor_1_out, xnor_2_out, xnor_3_out, xnor_4_out;

  xnor xnor_1 (xnor_1_out, C0, S0);
  xnor xnor_2 (xnor_2_out, C1, S1);
  xnor xnor_3 (xnor_3_out, C2, S2);
  xnor xnor_4 (xnor_4_out, C3, S3);
  and and_1 (out_9, xnor_1_out, xnor_2_out, xnor_3_out, xnor_4_out);
endmodule

// SSD1
module S_S_D (
  input  enable,
  input  z,
  input  y,
  input  x,
  input  w,
  output a,
  output b,
  output c,
  output d,
  output e,
  output f,
  output g,
  output DOT
);

  wire and_1_out, and_2_out, and_3_out, and_4_out, and_5_out, and_6_out, and_7_out, and_8_out, and_9_out,
       and_10_out, and_11_out, and_12_out, not_1_out, not_2_out, not_3_out, not_4_out, not_5_out, xor_1_out;

  not not_1 (not_1_out, x);
  not not_2 (not_2_out, z);
  not not_3 (not_3_out, y);
  not not_4 (not_4_out, x);
  xor xor_1 (xor_1_out, z, y);
  and and_1 (and_1_out, z, not_1_out);
  not not_5 (not_5_out, z);
  and and_2 (and_2_out, x, not_2_out);
  and and_3 (and_3_out, w, not_3_out);
  and and_4 (and_4_out, not_4_out, z);
  and and_5 (and_5_out, not_3_out, z);
  and and_6 (and_6_out, x, y, not_5_out);
  and and_7 (and_7_out, y, z);
  and and_8 (and_8_out, w, not_3_out);
  and and_9 (and_9_out, x, z);
  and and_10 (and_10_out, y, x);
  and and_11 (and_11_out, w, not_3_out);
  and and_12 (and_12_out, w, z);
  or or_1 (a, xor_1_out, and_1_out, w);
  or or_2 (b, y, x);
  or or_3 (c, and_2_out, w, y);
  or or_4 (d, and_3_out, and_4_out, and_5_out, and_6_out);
  or or_5 (e, and_4_out, and_5_out);
  or or_6 (f, and_7_out, and_8_out);
  or or_7 (g, and_9_out, and_10_out, and_11_out, and_12_out);

  assign DOT = enable;
endmodule

module CU (
  input  admin_lock,
  input  next,
  input  B0,
  input  B1,
  input  B2,
  input  B3,
  input  Edit_1,
  input  Edit,
  input  View,
  input  Admin,
  input  Reset,
  input  Key,
  input  Mode,
  input  Enable,
  output view_2,
  output Mode_1_2,
  output Lock_reset,
  output P5_enable,
  output P4_enable,
  output P3_enable,
  output P2_enable,
  output P1_enable,
  output P0_enable,
  output all_pins_entered,
  output Pass_4_enable,
  output Pass_3_enable,
  output Pass_2_enable,
  output Pass_1_enable,
  output Pass_0_enable,
  output S0,
  output S1,
  output S2,
  output S3,
  output C0,
  output C1,
  output C2,
  output C3
);

  wire and_1_out, and_2_out, and_3_out, d_ff_1_q, d_ff_3_q, d_ff_5_q, d_ff_7_q, d_ff_9_q, d_ff_11_q,
       not_1_out, or_1_out, or_2_out, or_3_out, or_4_out, or_5_out, or_6_out, or_7_out, or_8_out, or_10_out;

  or or_1 (or_1_out, Mode, and_2_out);
  or or_2 (or_2_out, or_1_out, Lock_reset, all_pins_entered);
  or or_3 (or_3_out, Enable, Admin);
  D_Flip_Flop d_ff_1 (.clk(or_2_out), .D(or_1_out), .Q(d_ff_1_q), .reset(Enable));  // open: Qn, preset, en
  or or_4 (or_4_out, Admin, Reset, and_3_out, Mode, Enable);
  and and_1 (and_1_out, admin_lock, next);
  and and_2 (and_2_out, Edit_1, admin_lock);
  and and_3 (and_3_out, admin_lock, View);
  or or_5 (or_5_out, Admin, Enable);
  or or_6 (or_6_out, and_1_out, Key);
  or or_7 (or_7_out, or_5_out, and_3_out);
  or or_8 (or_8_out, view_2, d_ff_1_q);
  T_Flip_Flop t_ff_1 (.clk(View), .T(View), .Q(view_2));  // open: Qn, preset, reset, en
  or or_9 (Lock_reset, Reset, Enable);
  D_Flip_Flop d_ff_2 (.clk(or_6_out), .D(all_pins_entered), .Q(P5_enable), .preset(or_4_out));  // open: Qn, en, reset
  D_Flip_Flop d_ff_3 (
    .clk(all_pins_entered), .D(d_ff_11_q), .Q(d_ff_3_q), .preset(and_3_out), .en(or_8_out), .reset(or_5_out));  // open: Qn
  D_Flip_Flop d_ff_4 (.clk(or_6_out), .D(P5_enable), .Q(P4_enable), .reset(or_4_out));  // open: Qn, preset, en
  D_Flip_Flop d_ff_5 (
    .clk(all_pins_entered), .D(d_ff_3_q), .Q(d_ff_5_q), .en(or_8_out), .reset(or_7_out));  // open: Qn, preset
  and and_4 (Pass_4_enable, or_8_out, d_ff_3_q);
  D_Flip_Flop d_ff_6 (.clk(or_6_out), .D(P4_enable), .Q(P3_enable), .reset(or_4_out));  // open: Qn, preset, en
  D_Flip_Flop d_ff_7 (
    .clk(all_pins_entered), .D(d_ff_5_q), .Q(d_ff_7_q), .en(or_8_out), .reset(or_7_out));  // open: Qn, preset
  and and_5 (Pass_3_enable, or_8_out, d_ff_5_q);
  D_Flip_Flop d_ff_8 (.clk(or_6_out), .D(P3_enable), .Q(P2_enable), .reset(or_4_out));  // open: Qn, preset, en
  D_Flip_Flop d_ff_9 (
    .clk(all_pins_entered), .D(d_ff_7_q), .Q(d_ff_9_q), .preset(or_3_out), .en(or_8_out), .reset(and_3_out));  // open: Qn
  and and_6 (Pass_2_enable, or_8_out, d_ff_7_q);
  D_Flip_Flop d_ff_10 (.clk(or_6_out), .D(P2_enable), .Q(P1_enable), .reset(or_4_out));  // open: Qn, preset, en
  D_Flip_Flop d_ff_11 (
    .clk(all_pins_entered), .D(d_ff_9_q), .Q(d_ff_11_q), .en(or_8_out), .reset(or_7_out));  // open: Qn, preset
  and and_7 (Pass_1_enable, or_8_out, d_ff_9_q);
  and and_8 (Pass_0_enable, or_8_out, d_ff_11_q);
  D_Flip_Flop d_ff_12 (.clk(or_6_out), .D(P0_enable), .Q(all_pins_entered), .reset(or_4_out));  // open: Qn, preset, en
  D_Flip_Flop d_ff_13 (.clk(or_6_out), .D(P1_enable), .Q(P0_enable), .reset(or_4_out));  // open: Qn, preset, en
  or or_10 (or_10_out, and_2_out, Mode);
  T_Flip_Flop t_ff_2 (.clk(or_10_out), .T(or_10_out), .Q(Mode_1_2), .reset(Lock_reset));  // open: Qn, preset, en
  and and_9 (S0, d_ff_1_q, B0);
  and and_10 (S1, d_ff_1_q, B1);
  and and_11 (S2, d_ff_1_q, B2);
  and and_12 (S3, d_ff_1_q, B3);
  not not_1 (not_1_out, d_ff_1_q);
  and and_13 (C0, not_1_out, B0);
  and and_14 (C2, not_1_out, B2);
  and and_15 (C1, not_1_out, B1);
  and and_16 (C3, not_1_out, B3);
endmodule

module Storage (
  input  Mode,
  input  Enable,
  input  B0,
  input  B1,
  input  B2,
  input  B3,
  input  P5_enable,
  input  P4_enable,
  input  P3_enable,
  input  P2_enable,
  input  P1_enable,
  input  P0_enable,
  output S0,
  output S1,
  output S2,
  output S3
);

  wire digit_0_1_s0, digit_0_1_s1, digit_0_1_s2, digit_0_1_s3, digit_0_2_s0, digit_0_2_s1, digit_0_2_s2,
       digit_0_2_s3, digit_1_1_s0, digit_1_1_s1, digit_1_1_s2, digit_1_1_s3, digit_2_1_s0, digit_2_1_s1,
       digit_2_1_s2, digit_2_1_s3, digit_2_2_s0, digit_2_2_s1, digit_2_2_s2, digit_2_2_s3, digit_4_1_s0,
       digit_4_1_s1, digit_4_1_s2, digit_4_1_s3;

  Digit_2 digit_2_1 (
    .B0(B0), .B1(B1), .B2(B2), .B3(B3), .Default(Enable), .Pin_enable(P5_enable), .Mode(Mode),
    .S0(digit_2_1_s0), .S1(digit_2_1_s1), .S2(digit_2_1_s2), .S3(digit_2_1_s3));
  digit_1 digit_1_1 (
    .B0(B0), .B1(B1), .B2(B2), .B3(B3), .Default(Enable), .Pin_enable(P4_enable), .Mode(Mode),
    .S0(digit_1_1_s0), .S1(digit_1_1_s1), .S2(digit_1_1_s2), .S3(digit_1_1_s3));
  digit_0 digit_0_1 (
    .B0(B0), .B1(B1), .B2(B2), .B3(B3), .Default(Enable), .Pin_enable(P3_enable), .Mode(Mode),
    .S0(digit_0_1_s0), .S1(digit_0_1_s1), .S2(digit_0_1_s2), .S3(digit_0_1_s3));
  digit_4 digit_4_1 (
    .B0(B0), .B1(B1), .B2(B2), .B3(B3), .Default(Enable), .Pin_enable(P2_enable), .Mode(Mode),
    .S0(digit_4_1_s0), .S1(digit_4_1_s1), .S2(digit_4_1_s2), .S3(digit_4_1_s3));
  Digit_2 digit_2_2 (
    .B0(B0), .B1(B1), .B2(B2), .B3(B3), .Default(Enable), .Pin_enable(P1_enable), .Mode(Mode),
    .S0(digit_2_2_s0), .S1(digit_2_2_s1), .S2(digit_2_2_s2), .S3(digit_2_2_s3));
  digit_0 digit_0_2 (
    .B0(B0), .B1(B1), .B2(B2), .B3(B3), .Default(Enable), .Pin_enable(P0_enable), .Mode(Mode),
    .S0(digit_0_2_s0), .S1(digit_0_2_s1), .S2(digit_0_2_s2), .S3(digit_0_2_s3));
  or or_1 (S0, digit_2_1_s0, digit_1_1_s0, digit_0_1_s0, digit_4_1_s0, digit_2_2_s0, digit_0_2_s0);
  or or_2 (S1, digit_2_1_s1, digit_1_1_s1, digit_0_1_s1, digit_4_1_s1, digit_2_2_s1, digit_0_2_s1);
  or or_3 (S2, digit_1_1_s2, digit_2_1_s2, digit_0_1_s2, digit_4_1_s2, digit_2_2_s2, digit_0_2_s2);
  or or_4 (S3, digit_2_1_s3, digit_1_1_s3, digit_0_1_s3, digit_4_1_s3, digit_2_2_s3, digit_0_2_s3);

  // Notes on the sheet:
  //   210420
endmodule

// OutGen
module Output_Storage (
  input  Mode,
  input  Reset,
  input  \input ,
  input  P4_enable,
  input  P3_enable,
  input  P2_enable,
  input  P1_enable,
  input  P0_enable,
  input  in_9,
  input  all_pins_entered,
  output Comparison_output,
  output Pin_status
);

  wire not_1_out, P0_comparison_q, P1_comparison_q, P2_comparison_q, P3_comparison_q, P4_comparison_2_q,
       P4_comparison_q;

  not not_1 (not_1_out, Mode);
  D_Flip_Flop #(.trigger("falling")) P4_comparison (
    .clk(P4_enable), .D(\input ), .Q(P4_comparison_q), .en(not_1_out), .reset(Reset));  // open: Qn, preset
  D_Flip_Flop #(.trigger("falling")) P3_comparison (
    .clk(P3_enable), .D(\input ), .Q(P3_comparison_q), .en(not_1_out), .reset(Reset));  // open: Qn, preset
  D_Flip_Flop #(.trigger("falling")) P2_comparison (
    .clk(P2_enable), .D(\input ), .Q(P2_comparison_q), .en(not_1_out), .reset(Reset));  // open: Qn, preset
  D_Flip_Flop #(.trigger("falling")) P1_comparison (
    .clk(P1_enable), .D(\input ), .Q(P1_comparison_q), .en(not_1_out), .reset(Reset));  // open: Qn, preset
  D_Flip_Flop #(.trigger("falling")) P0_comparison (
    .clk(P0_enable), .D(\input ), .Q(P0_comparison_q), .en(not_1_out), .reset(Reset));  // open: Qn, preset
  D_Flip_Flop #(.trigger("falling")) P4_comparison_2 (
    .clk(in_9), .D(\input ), .Q(P4_comparison_2_q), .en(not_1_out), .reset(Reset));  // open: Qn, preset
  and and_1 (Comparison_output, P4_comparison_q, P3_comparison_q, P2_comparison_q, P1_comparison_q, P0_comparison_q, P4_comparison_2_q);

  assign Pin_status = all_pins_entered;
endmodule

// SSD Out
module SSD_OUT (
  input  in_1,
  input  M,
  input  O,
  input  P5,
  input  admin,
  output B,
  output A,
  output F,
  output G,
  output E,
  output D,
  output C,
  output Dot
);

  wire and_1_out, and_2_out, and_3_out, and_4_out, and_5_out, and_6_out, not_1_out, not_2_out, not_3_out,
       not_4_out, not_5_out, not_6_out, not_7_out, or_1_out, or_2_out, or_3_out, or_4_out, or_5_out, or_6_out;

  and and_1 (and_1_out, admin, not_1_out);
  not not_1 (not_1_out, M);
  not not_2 (not_2_out, admin);
  not not_3 (not_3_out, O);
  and and_2 (and_2_out, not_3_out, M);
  not not_4 (not_4_out, admin);
  and and_3 (and_3_out, not_4_out, not_5_out);
  not not_5 (not_5_out, P5);
  and and_4 (and_4_out, not_4_out, O);
  not not_6 (not_6_out, M);
  not not_7 (not_7_out, P5);
  and and_5 (and_5_out, P5, O, not_1_out);
  and and_6 (and_6_out, not_2_out, P5, not_3_out, M);
  or or_1 (or_1_out, and_2_out, admin);
  or or_2 (or_2_out, admin, not_6_out, O, not_7_out);
  or or_3 (or_3_out, and_1_out, and_5_out);
  or or_4 (or_4_out, or_3_out, and_6_out);
  or or_5 (or_5_out, and_3_out, and_4_out, M);
  or or_6 (or_6_out, and_1_out, and_6_out);
  and and_7 (B, in_1, or_3_out);
  and and_8 (A, or_1_out, in_1);
  and and_9 (F, 1'b1, in_1);
  and and_10 (G, or_6_out, in_1);
  and and_11 (E, or_2_out, in_1);
  and and_12 (D, or_5_out, in_1);
  and and_13 (C, or_4_out, in_1);

  assign Dot = in_1;
endmodule

// P4
module Digit_2 (
  input  Default,
  input  Pin_enable,
  input  Mode,
  input  B0,
  input  B1,
  input  B2,
  input  B3,
  output S0,
  output S1,
  output S2,
  output S3
);

  wire d_ff_1_q, d_ff_2_q, d_ff_3_q, d_ff_4_q;

  D_Flip_Flop #(.trigger("falling")) d_ff_1 (
    .clk(Pin_enable), .D(B0), .Q(d_ff_1_q), .preset(Default), .en(Mode));  // open: Qn, reset
  D_Flip_Flop #(.trigger("falling")) d_ff_2 (
    .clk(Pin_enable), .D(B1), .Q(d_ff_2_q), .en(Mode), .reset(Default));  // open: Qn, preset
  D_Flip_Flop #(.trigger("falling")) d_ff_3 (
    .clk(Pin_enable), .D(B2), .Q(d_ff_3_q), .preset(Default), .en(Mode));  // open: Qn, reset
  D_Flip_Flop #(.trigger("falling")) d_ff_4 (
    .clk(Pin_enable), .D(B3), .Q(d_ff_4_q), .en(Mode), .reset(Default));  // open: Qn, preset
  and and_1 (S0, Pin_enable, d_ff_1_q);
  and and_2 (S1, Pin_enable, d_ff_2_q);
  and and_3 (S2, Pin_enable, d_ff_3_q);
  and and_4 (S3, Pin_enable, d_ff_4_q);

  // Notes on the sheet:
  //   21042
endmodule

// P3
module digit_1 (
  input  Default,
  input  Pin_enable,
  input  Mode,
  input  B0,
  input  B1,
  input  B2,
  input  B3,
  output S0,
  output S1,
  output S2,
  output S3
);

  wire d_ff_1_q, d_ff_2_q, d_ff_3_q, d_ff_4_q;

  D_Flip_Flop #(.trigger("falling")) d_ff_1 (
    .clk(Pin_enable), .D(B0), .Q(d_ff_1_q), .en(Mode), .reset(Default));  // open: Qn, preset
  D_Flip_Flop #(.trigger("falling")) d_ff_2 (
    .clk(Pin_enable), .D(B1), .Q(d_ff_2_q), .en(Mode), .reset(Default));  // open: Qn, preset
  D_Flip_Flop #(.trigger("falling")) d_ff_3 (
    .clk(Pin_enable), .D(B2), .Q(d_ff_3_q), .preset(Default), .en(Mode));  // open: Qn, reset
  D_Flip_Flop #(.trigger("falling")) d_ff_4 (
    .clk(Pin_enable), .D(B3), .Q(d_ff_4_q), .en(Mode), .reset(Default));  // open: Qn, preset
  and and_1 (S0, Pin_enable, d_ff_1_q);
  and and_2 (S1, Pin_enable, d_ff_2_q);
  and and_3 (S2, Pin_enable, d_ff_3_q);
  and and_4 (S3, Pin_enable, d_ff_4_q);

  // Notes on the sheet:
  //   21042
endmodule

// P2
module digit_0 (
  input  Default,
  input  Pin_enable,
  input  Mode,
  input  B0,
  input  B1,
  input  B2,
  input  B3,
  output S0,
  output S1,
  output S2,
  output S3
);

  wire d_ff_1_q, d_ff_2_q, d_ff_3_q, d_ff_4_q;

  D_Flip_Flop #(.trigger("falling")) d_ff_1 (
    .clk(Pin_enable), .D(B0), .Q(d_ff_1_q), .preset(Default), .en(Mode));  // open: Qn, reset
  D_Flip_Flop #(.trigger("falling")) d_ff_2 (
    .clk(Pin_enable), .D(B1), .Q(d_ff_2_q), .preset(Default), .en(Mode));  // open: Qn, reset
  D_Flip_Flop #(.trigger("falling")) d_ff_3 (
    .clk(Pin_enable), .D(B2), .Q(d_ff_3_q), .en(Mode), .reset(Default));  // open: Qn, preset
  D_Flip_Flop #(.trigger("falling")) d_ff_4 (
    .clk(Pin_enable), .D(B3), .Q(d_ff_4_q), .en(Mode), .reset(Default));  // open: Qn, preset
  and and_1 (S0, Pin_enable, d_ff_1_q);
  and and_2 (S1, Pin_enable, d_ff_2_q);
  and and_3 (S2, Pin_enable, d_ff_3_q);
  and and_4 (S3, Pin_enable, d_ff_4_q);

  // Notes on the sheet:
  //   21042
endmodule

// P1
module digit_4 (
  input  Default,
  input  Pin_enable,
  input  Mode,
  input  B0,
  input  B1,
  input  B2,
  input  B3,
  output S0,
  output S1,
  output S2,
  output S3
);

  wire d_ff_1_q, d_ff_2_q, d_ff_3_q, d_ff_4_q;

  D_Flip_Flop #(.trigger("falling")) d_ff_1 (
    .clk(Pin_enable), .D(B0), .Q(d_ff_1_q), .preset(Default), .en(Mode));  // open: Qn, reset
  D_Flip_Flop #(.trigger("falling")) d_ff_2 (
    .clk(Pin_enable), .D(B1), .Q(d_ff_2_q), .preset(Default), .en(Mode));  // open: Qn, reset
  D_Flip_Flop #(.trigger("falling")) d_ff_3 (
    .clk(Pin_enable), .D(B2), .Q(d_ff_3_q), .preset(Default), .en(Mode));  // open: Qn, reset
  D_Flip_Flop #(.trigger("falling")) d_ff_4 (
    .clk(Pin_enable), .D(B3), .Q(d_ff_4_q), .en(Mode), .reset(Default));  // open: Qn, preset
  and and_1 (S0, Pin_enable, d_ff_1_q);
  and and_2 (S1, Pin_enable, d_ff_2_q);
  and and_3 (S2, Pin_enable, d_ff_3_q);
  and and_4 (S3, Pin_enable, d_ff_4_q);

  // Notes on the sheet:
  //   21042
endmodule

// P0
module digit_3 (
  input  \default ,
  input  pin_enable,
  input  mode,
  input  B0,
  input  B1,
  input  B2,
  input  B3,
  output S0,
  output S1,
  output S2,
  output S3
);

  wire d_ff_1_q, d_ff_2_q, d_ff_3_q, d_ff_4_q;

  D_Flip_Flop #(.trigger("falling")) d_ff_1 (
    .clk(pin_enable), .D(B0), .Q(d_ff_1_q), .en(mode), .reset(\default ));  // open: Qn, preset
  D_Flip_Flop #(.trigger("falling")) d_ff_2 (
    .clk(pin_enable), .D(B1), .Q(d_ff_2_q), .preset(\default ), .en(mode));  // open: Qn, reset
  D_Flip_Flop #(.trigger("falling")) d_ff_3 (
    .clk(pin_enable), .D(B2), .Q(d_ff_3_q), .preset(\default ), .en(mode));  // open: Qn, reset
  D_Flip_Flop #(.trigger("falling")) d_ff_4 (
    .clk(pin_enable), .D(B3), .Q(d_ff_4_q), .en(mode), .reset(\default ));  // open: Qn, preset
  and and_1 (S0, pin_enable, d_ff_1_q);
  and and_2 (S1, pin_enable, d_ff_2_q);
  and and_3 (S2, pin_enable, d_ff_3_q);
  and and_4 (S3, pin_enable, d_ff_4_q);

  // Notes on the sheet:
  //   21042
endmodule

module No_value_pin (
  input  in_1,
  input  in_2,
  input  in_3,
  input  B0,
  input  B1,
  input  B2,
  input  B3,
  output out_8,
  output out_9,
  output out_10,
  output out_11
);

  wire d_ff_1_q, d_ff_2_q, d_ff_3_q, d_ff_4_q;

  D_Flip_Flop #(.trigger("falling")) d_ff_1 (
    .clk(in_2), .D(B0), .Q(d_ff_1_q), .en(in_3), .reset(in_1));  // open: Qn, preset
  D_Flip_Flop #(.trigger("falling")) d_ff_2 (
    .clk(in_2), .D(B1), .Q(d_ff_2_q), .en(in_3), .reset(in_1));  // open: Qn, preset
  D_Flip_Flop #(.trigger("falling")) d_ff_3 (
    .clk(in_2), .D(B2), .Q(d_ff_3_q), .en(in_3), .reset(in_1));  // open: Qn, preset
  D_Flip_Flop #(.trigger("falling")) d_ff_4 (
    .clk(in_2), .D(B3), .Q(d_ff_4_q), .en(in_3), .reset(in_1));  // open: Qn, preset
  and and_1 (out_8, in_2, d_ff_1_q);
  and and_2 (out_9, in_2, d_ff_2_q);
  and and_3 (out_10, in_2, d_ff_3_q);
  and and_4 (out_11, in_2, d_ff_4_q);
endmodule

// Storage 2
module storage_2 (
  input  Mode,
  input  Enable,
  input  B0,
  input  B1,
  input  B2,
  input  B3,
  input  P5_enable,
  input  P4_enable,
  input  P3_enable,
  input  P2_enable,
  input  P1_enable,
  input  P0_enable,
  output S0,
  output S1,
  output S2,
  output S3
);

  wire digit_2_1_s0, digit_2_1_s1, digit_2_1_s2, digit_2_1_s3, digit_2_2_s0, digit_2_2_s1, digit_2_2_s2,
       digit_2_2_s3, digit_2_3_s0, digit_2_3_s1, digit_2_3_s2, digit_2_3_s3, digit_2_4_s0, digit_2_4_s1,
       digit_2_4_s2, digit_2_4_s3, digit_2_5_s0, digit_2_5_s1, digit_2_5_s2, digit_2_5_s3, digit_2_6_s0,
       digit_2_6_s1, digit_2_6_s2, digit_2_6_s3;

  Digit_2 digit_2_1 (
    .B0(B0), .B1(B1), .B2(B2), .B3(B3), .Default(Enable), .Pin_enable(P5_enable), .Mode(Mode),
    .S0(digit_2_1_s0), .S1(digit_2_1_s1), .S2(digit_2_1_s2), .S3(digit_2_1_s3));
  Digit_2 digit_2_2 (
    .B0(B0), .B1(B1), .B2(B2), .B3(B3), .Default(Enable), .Pin_enable(P4_enable), .Mode(Mode),
    .S0(digit_2_2_s0), .S1(digit_2_2_s1), .S2(digit_2_2_s2), .S3(digit_2_2_s3));
  Digit_2 digit_2_3 (
    .B0(B0), .B1(B1), .B2(B2), .B3(B3), .Default(Enable), .Pin_enable(P3_enable), .Mode(Mode),
    .S0(digit_2_3_s0), .S1(digit_2_3_s1), .S2(digit_2_3_s2), .S3(digit_2_3_s3));
  Digit_2 digit_2_4 (
    .B0(B0), .B1(B1), .B2(B2), .B3(B3), .Default(Enable), .Pin_enable(P2_enable), .Mode(Mode),
    .S0(digit_2_4_s0), .S1(digit_2_4_s1), .S2(digit_2_4_s2), .S3(digit_2_4_s3));
  Digit_2 digit_2_5 (
    .B0(B0), .B1(B1), .B2(B2), .B3(B3), .Default(Enable), .Pin_enable(P1_enable), .Mode(Mode),
    .S0(digit_2_5_s0), .S1(digit_2_5_s1), .S2(digit_2_5_s2), .S3(digit_2_5_s3));
  Digit_2 digit_2_6 (
    .B0(B0), .B1(B1), .B2(B2), .B3(B3), .Default(Enable), .Pin_enable(P0_enable), .Mode(Mode),
    .S0(digit_2_6_s0), .S1(digit_2_6_s1), .S2(digit_2_6_s2), .S3(digit_2_6_s3));
  or or_1 (S0, digit_2_1_s0, digit_2_2_s0, digit_2_3_s0, digit_2_4_s0, digit_2_5_s0, digit_2_6_s0);
  or or_2 (S1, digit_2_1_s1, digit_2_2_s1, digit_2_3_s1, digit_2_4_s1, digit_2_5_s1, digit_2_6_s1);
  or or_3 (S2, digit_2_2_s2, digit_2_1_s2, digit_2_3_s2, digit_2_4_s2, digit_2_5_s2, digit_2_6_s2);
  or or_4 (S3, digit_2_1_s3, digit_2_2_s3, digit_2_3_s3, digit_2_4_s3, digit_2_5_s3, digit_2_6_s3);

  // Notes on the sheet:
  //   222222
endmodule

module storage_3 (
  input  Mode,
  input  Enable,
  input  B0,
  input  B1,
  input  B2,
  input  B3,
  input  P5_enable,
  input  P4_enable,
  input  P3_enable,
  input  P2_enable,
  input  P1_enable,
  input  P0_enable,
  output S0,
  output S1,
  output S2,
  output S3
);

  wire digit_1_1_s0, digit_1_1_s1, digit_1_1_s2, digit_1_1_s3, digit_1_2_s0, digit_1_2_s1, digit_1_2_s2,
       digit_1_2_s3, digit_2_1_s0, digit_2_1_s1, digit_2_1_s2, digit_2_1_s3, digit_3_1_s0, digit_3_1_s1,
       digit_3_1_s2, digit_3_1_s3, digit_4_1_s0, digit_4_1_s1, digit_4_1_s2, digit_4_1_s3, digit_5_1_s0,
       digit_5_1_s1, digit_5_1_s2, digit_5_1_s3;

  digit_1 digit_1_1 (
    .B0(B0), .B1(B1), .B2(B2), .B3(B3), .Default(Enable), .Pin_enable(P5_enable), .Mode(Mode),
    .S0(digit_1_1_s0), .S1(digit_1_1_s1), .S2(digit_1_1_s2), .S3(digit_1_1_s3));
  Digit_2 digit_2_1 (
    .B0(B0), .B1(B1), .B2(B2), .B3(B3), .Default(Enable), .Pin_enable(P4_enable), .Mode(Mode),
    .S0(digit_2_1_s0), .S1(digit_2_1_s1), .S2(digit_2_1_s2), .S3(digit_2_1_s3));
  digit_3 digit_3_1 (
    .B0(B0), .B1(B1), .B2(B2), .B3(B3), .\default (Enable), .pin_enable(P3_enable), .mode(Mode),
    .S0(digit_3_1_s0), .S1(digit_3_1_s1), .S2(digit_3_1_s2), .S3(digit_3_1_s3));
  digit_4 digit_4_1 (
    .B0(B0), .B1(B1), .B2(B2), .B3(B3), .Default(Enable), .Pin_enable(P2_enable), .Mode(Mode),
    .S0(digit_4_1_s0), .S1(digit_4_1_s1), .S2(digit_4_1_s2), .S3(digit_4_1_s3));
  digit_5 digit_5_1 (
    .B0(B0), .B1(B1), .B2(B2), .B3(B3), .Default(Enable), .Pin_enable(P1_enable), .Mode(Mode),
    .S0(digit_5_1_s0), .S1(digit_5_1_s1), .S2(digit_5_1_s2), .S3(digit_5_1_s3));
  digit_1 digit_1_2 (
    .B0(B0), .B1(B1), .B2(B2), .B3(B3), .Default(Enable), .Pin_enable(P0_enable), .Mode(Mode),
    .S0(digit_1_2_s0), .S1(digit_1_2_s1), .S2(digit_1_2_s2), .S3(digit_1_2_s3));
  or or_1 (S0, digit_1_1_s0, digit_2_1_s0, digit_3_1_s0, digit_4_1_s0, digit_5_1_s0, digit_1_2_s0);
  or or_2 (S1, digit_1_1_s1, digit_2_1_s1, digit_3_1_s1, digit_4_1_s1, digit_5_1_s1, digit_1_2_s1);
  or or_3 (S2, digit_2_1_s2, digit_1_1_s2, digit_3_1_s2, digit_4_1_s2, digit_5_1_s2, digit_1_2_s2);
  or or_4 (S3, digit_1_1_s3, digit_2_1_s3, digit_3_1_s3, digit_4_1_s3, digit_5_1_s3, digit_1_2_s3);

  // Notes on the sheet:
  //   123451
endmodule

// Main Storage
module Big_store (
  input  in_1,
  input  enable,
  input  admin,
  input  B0,
  input  B1,
  input  B2,
  input  B3,
  input  P5,
  input  P4,
  input  P3,
  input  P2,
  input  P1,
  input  P0,
  input  in_14,
  input  in_15,
  input  in_16,
  input  in_17,
  input  in_18,
  output S0,
  output S1,
  output S2,
  output S3,
  output out_23,
  output out_24,
  output out_25,
  output out_26,
  output out_27,
  output out_28,
  output out_29,
  output out_30,
  output out_31,
  output out_32,
  output out_33,
  output out_34,
  output out_35,
  output out_36,
  output out_37,
  output out_38,
  output admin_2,
  output out_40,
  output out_41,
  output out_42,
  output out_43
);

  wire admin_storage_1_s0, admin_storage_1_s1, admin_storage_1_s2, admin_storage_1_s3, and_1_out, and_2_out,
       and_3_out, and_4_out, and_5_out;

  and and_1 (and_1_out, in_1, in_14);
  and and_2 (and_2_out, in_1, in_15);
  and and_3 (and_3_out, in_1, in_16);
  and and_4 (and_4_out, in_1, in_17);
  and and_5 (and_5_out, in_1, in_18);
  Storage storage_1 (
    .B0(B0), .B1(B1), .B2(B2), .B3(B3), .P5_enable(P5), .P4_enable(P4), .P3_enable(P3), .P2_enable(P2),
    .P1_enable(P1), .P0_enable(P0), .Mode(and_1_out), .Enable(enable), .S0(S0), .S1(S1), .S2(S2), .S3(S3));
  storage_2 storage_2_1 (
    .B0(B0), .B1(B1), .B2(B2), .B3(B3), .P5_enable(P5), .P4_enable(P4), .P3_enable(P3), .P2_enable(P2),
    .P1_enable(P1), .P0_enable(P0), .Mode(and_2_out), .Enable(enable), .S0(out_23), .S1(out_24), .S2(out_25),
    .S3(out_26));
  storage_3 storage_3_1 (
    .B0(B0), .B1(B1), .B2(B2), .B3(B3), .P5_enable(P5), .P4_enable(P4), .P3_enable(P3), .P2_enable(P2),
    .P1_enable(P1), .P0_enable(P0), .Mode(and_3_out), .Enable(enable), .S0(out_27), .S1(out_28), .S2(out_29),
    .S3(out_30));
  Fillable_stoage fillable_stoage_1 (
    .B0(B0), .B1(B1), .B2(B2), .B3(B3), .P5_enable(P5), .P4_enable(P4), .P3_enable(P3), .P2_enable(P2),
    .P1_enable(P1), .P0_enable(P0), .Mode(and_4_out), .Enable(enable), .S0(out_31), .S1(out_32), .S2(out_33),
    .S3(out_34));
  Fillable_stoage fillable_stoage_2 (
    .B0(B0), .B1(B1), .B2(B2), .B3(B3), .P5_enable(P5), .P4_enable(P4), .P3_enable(P3), .P2_enable(P2),
    .P1_enable(P1), .P0_enable(P0), .Mode(and_5_out), .Enable(enable), .S0(out_35), .S1(out_36), .S2(out_37),
    .S3(out_38));
  Admin_storage admin_storage_1 (
    .P5_enable(P5), .P4_enable(P4), .P3_enable(P3), .P2_enable(P2), .P1_enable(P1), .in_12(P0),
    .Enable(enable), .S0(admin_storage_1_s0), .S1(admin_storage_1_s1), .S2(admin_storage_1_s2),
    .S3(admin_storage_1_s3));  // open: B0, B1, B2, B3, Mode
  T_Flip_Flop t_ff_1 (.clk(admin), .T(admin), .Q(admin_2), .reset(enable));  // open: Qn, preset, en
  and and_6 (out_40, admin_2, admin_storage_1_s0);
  and and_7 (out_41, admin_2, admin_storage_1_s1);
  and and_8 (out_42, admin_2, admin_storage_1_s2);
  and and_9 (out_43, admin_2, admin_storage_1_s3);
endmodule

module digit_5 (
  input  Default,
  input  Pin_enable,
  input  Mode,
  input  B0,
  input  B1,
  input  B2,
  input  B3,
  output S0,
  output S1,
  output S2,
  output S3
);

  wire d_ff_1_q, d_ff_2_q, d_ff_3_q, d_ff_4_q;

  D_Flip_Flop #(.trigger("falling")) d_ff_1 (
    .clk(Pin_enable), .D(B0), .Q(d_ff_1_q), .en(Mode), .reset(Default));  // open: Qn, preset
  D_Flip_Flop #(.trigger("falling")) d_ff_2 (
    .clk(Pin_enable), .D(B1), .Q(d_ff_2_q), .en(Mode), .reset(Default));  // open: Qn, preset
  D_Flip_Flop #(.trigger("falling")) d_ff_3 (
    .clk(Pin_enable), .D(B2), .Q(d_ff_3_q), .en(Mode), .reset(Default));  // open: Qn, preset
  D_Flip_Flop #(.trigger("falling")) d_ff_4 (
    .clk(Pin_enable), .D(B3), .Q(d_ff_4_q), .preset(Default), .en(Mode));  // open: Qn, reset
  and and_1 (S0, Pin_enable, d_ff_1_q);
  and and_2 (S1, Pin_enable, d_ff_2_q);
  and and_3 (S2, Pin_enable, d_ff_3_q);
  and and_4 (S3, Pin_enable, d_ff_4_q);

  // Notes on the sheet:
  //   21042
endmodule

module big_comparator (
  input  in_1,
  input  in_2,
  input  in_3,
  input  in_4,
  input  in_5,
  input  in_6,
  input  in_7,
  input  in_8,
  input  in_9,
  input  in_10,
  input  in_11,
  input  in_12,
  input  in_13,
  input  in_14,
  input  in_15,
  input  in_16,
  output out_17,
  output out_18,
  output out_19
);

  Comparator comparator_1 (
    .C0(in_1), .C1(in_2), .C2(in_3), .C3(in_4), .S0(in_5), .S1(in_6), .S2(in_7), .S3(in_8), .out_9(out_17));
  Comparator comparator_2 (
    .C0(in_1), .C1(in_2), .C2(in_3), .C3(in_4), .S0(in_9), .S1(in_10), .S2(in_11), .S3(in_12), .out_9(out_18));
  Comparator comparator_3 (
    .C0(in_1), .C1(in_2), .C2(in_3), .C3(in_4), .S0(in_13), .S1(in_14), .S2(in_15), .S3(in_16), .out_9(out_19));
endmodule

// Output generator
module big_outputgen (
  input  Mode,
  input  Reset,
  input  enter,
  input  output_1,
  input  output_2,
  input  output_3,
  input  output_4,
  input  output_5,
  input  p5,
  input  P4,
  input  p3,
  input  p2,
  input  p1,
  input  p0,
  input  all_pins_entered,
  output Ouput,
  output All_pins_entered_2
);

  wire output_storage_1_comparison_output, output_storage_2_comparison_output,
       output_storage_3_comparison_output, output_storage_4_comparison_output,
       output_storage_5_comparison_output;

  Output_Storage output_storage_1 (
    .\input (output_1), .P4_enable(p5), .P3_enable(P4), .P2_enable(p3), .P1_enable(p2), .P0_enable(p1),
    .in_9(p0), .all_pins_entered(all_pins_entered), .Mode(Mode), .Reset(Reset),
    .Comparison_output(output_storage_1_comparison_output));  // open: Pin_status
  Output_Storage output_storage_2 (
    .\input (output_2), .P4_enable(p5), .P3_enable(P4), .P2_enable(p3), .P1_enable(p2), .P0_enable(p1),
    .in_9(p0), .all_pins_entered(all_pins_entered), .Mode(Mode), .Reset(Reset),
    .Comparison_output(output_storage_2_comparison_output));  // open: Pin_status
  Output_Storage output_storage_3 (
    .\input (output_3), .P4_enable(p5), .P3_enable(P4), .P2_enable(p3), .P1_enable(p2), .P0_enable(p1),
    .in_9(p0), .all_pins_entered(all_pins_entered), .Mode(Mode), .Reset(Reset),
    .Comparison_output(output_storage_3_comparison_output));  // open: Pin_status
  Output_Storage output_storage_4 (
    .\input (output_4), .P4_enable(p5), .P3_enable(P4), .P2_enable(p3), .P1_enable(p2), .P0_enable(p1),
    .in_9(p0), .all_pins_entered(all_pins_entered), .Mode(Mode), .Reset(Reset),
    .Comparison_output(output_storage_4_comparison_output));  // open: Pin_status
  Output_Storage output_storage_5 (
    .\input (output_5), .P4_enable(p5), .P3_enable(P4), .P2_enable(p3), .P1_enable(p2), .P0_enable(p1),
    .in_9(p0), .all_pins_entered(all_pins_entered), .Mode(Mode), .Reset(Reset),
    .Comparison_output(output_storage_5_comparison_output), .Pin_status(All_pins_entered_2));
  or or_1 (Ouput, output_storage_1_comparison_output, output_storage_4_comparison_output, output_storage_2_comparison_output, output_storage_5_comparison_output, output_storage_3_comparison_output);
endmodule

module Fillable_stoage (
  input  Mode,
  input  Enable,
  input  B0,
  input  B1,
  input  B2,
  input  B3,
  input  P5_enable,
  input  P4_enable,
  input  P3_enable,
  input  P2_enable,
  input  P1_enable,
  input  P0_enable,
  output S0,
  output S1,
  output S2,
  output S3
);

  wire no_value_pin_1_out_8, no_value_pin_1_out_9, no_value_pin_1_out_10, no_value_pin_1_out_11,
       no_value_pin_2_out_8, no_value_pin_2_out_9, no_value_pin_2_out_10, no_value_pin_2_out_11,
       no_value_pin_3_out_8, no_value_pin_3_out_9, no_value_pin_3_out_10, no_value_pin_3_out_11,
       no_value_pin_4_out_8, no_value_pin_4_out_9, no_value_pin_4_out_10, no_value_pin_4_out_11,
       no_value_pin_5_out_8, no_value_pin_5_out_9, no_value_pin_5_out_10, no_value_pin_5_out_11,
       no_value_pin_6_out_8, no_value_pin_6_out_9, no_value_pin_6_out_10, no_value_pin_6_out_11;

  No_value_pin no_value_pin_1 (
    .B0(B0), .B1(B1), .B2(B2), .B3(B3), .in_1(Enable), .in_2(P5_enable), .in_3(Mode),
    .out_8(no_value_pin_1_out_8), .out_9(no_value_pin_1_out_9), .out_10(no_value_pin_1_out_10),
    .out_11(no_value_pin_1_out_11));
  No_value_pin no_value_pin_2 (
    .B0(B0), .B1(B1), .B2(B2), .B3(B3), .in_1(Enable), .in_2(P4_enable), .in_3(Mode),
    .out_8(no_value_pin_2_out_8), .out_9(no_value_pin_2_out_9), .out_10(no_value_pin_2_out_10),
    .out_11(no_value_pin_2_out_11));
  No_value_pin no_value_pin_3 (
    .B0(B0), .B1(B1), .B2(B2), .B3(B3), .in_1(Enable), .in_2(P3_enable), .in_3(Mode),
    .out_8(no_value_pin_3_out_8), .out_9(no_value_pin_3_out_9), .out_10(no_value_pin_3_out_10),
    .out_11(no_value_pin_3_out_11));
  No_value_pin no_value_pin_4 (
    .B0(B0), .B1(B1), .B2(B2), .B3(B3), .in_1(Enable), .in_2(P2_enable), .in_3(Mode),
    .out_8(no_value_pin_4_out_8), .out_9(no_value_pin_4_out_9), .out_10(no_value_pin_4_out_10),
    .out_11(no_value_pin_4_out_11));
  No_value_pin no_value_pin_5 (
    .B0(B0), .B1(B1), .B2(B2), .B3(B3), .in_1(Enable), .in_2(P1_enable), .in_3(Mode),
    .out_8(no_value_pin_5_out_8), .out_9(no_value_pin_5_out_9), .out_10(no_value_pin_5_out_10),
    .out_11(no_value_pin_5_out_11));
  No_value_pin no_value_pin_6 (
    .B0(B0), .B1(B1), .B2(B2), .B3(B3), .in_1(Enable), .in_2(P0_enable), .in_3(Mode),
    .out_8(no_value_pin_6_out_8), .out_9(no_value_pin_6_out_9), .out_10(no_value_pin_6_out_10),
    .out_11(no_value_pin_6_out_11));
  or or_1 (S0, no_value_pin_1_out_8, no_value_pin_2_out_8, no_value_pin_3_out_8, no_value_pin_4_out_8, no_value_pin_5_out_8, no_value_pin_6_out_8);
  or or_2 (S1, no_value_pin_1_out_9, no_value_pin_2_out_9, no_value_pin_3_out_9, no_value_pin_4_out_9, no_value_pin_5_out_9, no_value_pin_6_out_9);
  or or_3 (S2, no_value_pin_2_out_10, no_value_pin_1_out_10, no_value_pin_3_out_10, no_value_pin_4_out_10, no_value_pin_5_out_10, no_value_pin_6_out_10);
  or or_4 (S3, no_value_pin_1_out_11, no_value_pin_2_out_11, no_value_pin_3_out_11, no_value_pin_4_out_11, no_value_pin_5_out_11, no_value_pin_6_out_11);

  // Notes on the sheet:
  //   21042
endmodule

module Admin_storage (
  input  Mode,
  input  Enable,
  input  B0,
  input  B1,
  input  B2,
  input  B3,
  input  P5_enable,
  input  P4_enable,
  input  P3_enable,
  input  P2_enable,
  input  P1_enable,
  input  in_12,
  output S0,
  output S1,
  output S2,
  output S3
);

  wire digit_0_1_s0, digit_0_1_s1, digit_0_1_s2, digit_0_1_s3, digit_0_2_s0, digit_0_2_s1, digit_0_2_s2,
       digit_0_2_s3, digit_0_3_s0, digit_0_3_s1, digit_0_3_s2, digit_0_3_s3, digit_0_4_s0, digit_0_4_s1,
       digit_0_4_s2, digit_0_4_s3, digit_0_5_s0, digit_0_5_s1, digit_0_5_s2, digit_0_5_s3, digit_0_6_s0,
       digit_0_6_s1, digit_0_6_s2, digit_0_6_s3;

  digit_0 digit_0_1 (
    .B0(B0), .B1(B1), .B2(B2), .B3(B3), .Default(Enable), .Pin_enable(P5_enable), .Mode(Mode),
    .S0(digit_0_1_s0), .S1(digit_0_1_s1), .S2(digit_0_1_s2), .S3(digit_0_1_s3));
  digit_0 digit_0_2 (
    .B0(B0), .B1(B1), .B2(B2), .B3(B3), .Default(Enable), .Pin_enable(P4_enable), .Mode(Mode),
    .S0(digit_0_2_s0), .S1(digit_0_2_s1), .S2(digit_0_2_s2), .S3(digit_0_2_s3));
  digit_0 digit_0_3 (
    .B0(B0), .B1(B1), .B2(B2), .B3(B3), .Default(Enable), .Pin_enable(P3_enable), .Mode(Mode),
    .S0(digit_0_3_s0), .S1(digit_0_3_s1), .S2(digit_0_3_s2), .S3(digit_0_3_s3));
  digit_0 digit_0_4 (
    .B0(B0), .B1(B1), .B2(B2), .B3(B3), .Default(Enable), .Pin_enable(P2_enable), .Mode(Mode),
    .S0(digit_0_4_s0), .S1(digit_0_4_s1), .S2(digit_0_4_s2), .S3(digit_0_4_s3));
  digit_0 digit_0_5 (
    .B0(B0), .B1(B1), .B2(B2), .B3(B3), .Default(Enable), .Pin_enable(P1_enable), .Mode(Mode),
    .S0(digit_0_5_s0), .S1(digit_0_5_s1), .S2(digit_0_5_s2), .S3(digit_0_5_s3));
  digit_0 digit_0_6 (
    .B0(B0), .B1(B1), .B2(B2), .B3(B3), .Default(Enable), .Pin_enable(in_12), .Mode(Mode), .S0(digit_0_6_s0),
    .S1(digit_0_6_s1), .S2(digit_0_6_s2), .S3(digit_0_6_s3));
  or or_1 (S0, digit_0_1_s0, digit_0_2_s0, digit_0_3_s0, digit_0_4_s0, digit_0_5_s0, digit_0_6_s0);
  or or_2 (S1, digit_0_1_s1, digit_0_2_s1, digit_0_3_s1, digit_0_4_s1, digit_0_5_s1, digit_0_6_s1);
  or or_3 (S2, digit_0_2_s2, digit_0_1_s2, digit_0_3_s2, digit_0_4_s2, digit_0_5_s2, digit_0_6_s2);
  or or_4 (S3, digit_0_1_s3, digit_0_2_s3, digit_0_3_s3, digit_0_4_s3, digit_0_5_s3, digit_0_6_s3);

  // Notes on the sheet:
  //   000000
endmodule

module Admin_enable (
  input  admin_toggle,
  input  Reset,
  input  \input ,
  input  P5_enable,
  input  P4_enable,
  input  P3_enable,
  input  P2_enable,
  input  P1_enable,
  input  P0_enable,
  output Comparison_output
);

  wire and_1_out, P0_comparison_q, P1_comparison_q, P2_comparison_q, P3_comparison_q, P4_comparison_2_q,
       P4_comparison_q, xor_1_out;

  xor xor_1 (xor_1_out, admin_toggle, and_1_out);
  D_Flip_Flop #(.trigger("falling")) P4_comparison (
    .clk(P5_enable), .D(\input ), .Q(P4_comparison_q), .en(xor_1_out), .reset(Reset));  // open: Qn, preset
  D_Flip_Flop #(.trigger("falling")) P3_comparison (
    .clk(P4_enable), .D(\input ), .Q(P3_comparison_q), .en(xor_1_out), .reset(Reset));  // open: Qn, preset
  D_Flip_Flop #(.trigger("falling")) P2_comparison (
    .clk(P3_enable), .D(\input ), .Q(P2_comparison_q), .en(xor_1_out), .reset(Reset));  // open: Qn, preset
  D_Flip_Flop #(.trigger("falling")) P1_comparison (
    .clk(P2_enable), .D(\input ), .Q(P1_comparison_q), .en(xor_1_out), .reset(Reset));  // open: Qn, preset
  D_Flip_Flop #(.trigger("falling")) P0_comparison (
    .clk(P1_enable), .D(\input ), .Q(P0_comparison_q), .en(xor_1_out), .reset(Reset));  // open: Qn, preset
  D_Flip_Flop #(.trigger("falling")) P4_comparison_2 (
    .clk(P0_enable), .D(\input ), .Q(P4_comparison_2_q), .en(xor_1_out), .reset(Reset));  // open: Qn, preset
  and and_1 (and_1_out, P4_comparison_q, P3_comparison_q, P2_comparison_q, P1_comparison_q, P0_comparison_q, P4_comparison_2_q);
  and and_2 (Comparison_output, admin_toggle, and_1_out);
endmodule

module Admin_controller (
  input  admin_toggle,
  input  reset,
  input  in_3,
  input  in_4,
  input  in_5,
  input  in_6,
  input  in_7,
  input  in_8,
  input  in_9,
  input  in_10,
  input  P5_enable,
  input  P4_enable,
  input  P3_enable,
  input  P2_enable,
  input  P1_enable,
  input  P0_enable,
  output out_17
);

  wire comparator_1_out_9;

  Comparator comparator_1 (
    .C0(in_3), .C1(in_4), .C2(in_5), .C3(in_6), .S0(in_7), .S1(in_8), .S2(in_9), .S3(in_10),
    .out_9(comparator_1_out_9));
  Admin_enable admin_enable_1 (
    .\input (comparator_1_out_9), .P5_enable(P5_enable), .P4_enable(P4_enable), .P3_enable(P3_enable),
    .P2_enable(P2_enable), .P1_enable(P1_enable), .P0_enable(P0_enable), .admin_toggle(admin_toggle),
    .Reset(reset), .Comparison_output(out_17));
endmodule

module Password_Display (
  input  P4,
  input  P3,
  input  P2,
  input  P1,
  input  P0,
  input  in_6,
  input  in_7,
  input  in_8,
  input  in_9,
  input  in_10,
  input  in_11,
  input  in_12,
  input  in_13,
  input  in_14,
  input  in_15,
  input  in_16,
  input  in_17,
  input  in_18,
  input  in_19,
  input  in_20,
  input  in_21,
  input  in_22,
  input  in_23,
  input  in_24,
  input  in_25,
  output D0,
  output D1,
  output D2,
  output D3
);

  wire and_1_out, and_2_out, and_3_out, and_4_out, and_5_out, and_6_out, and_7_out, and_8_out, and_9_out,
       and_10_out, and_11_out, and_12_out, and_13_out, and_14_out, and_15_out, and_16_out, and_17_out,
       and_18_out, and_19_out, and_20_out;

  and and_1 (and_1_out, P4, in_6);
  and and_2 (and_2_out, P4, in_7);
  and and_3 (and_3_out, P4, in_8);
  and and_4 (and_4_out, P4, in_9);
  and and_5 (and_5_out, P3, in_10);
  and and_6 (and_6_out, P3, in_11);
  and and_7 (and_7_out, P3, in_12);
  and and_8 (and_8_out, P3, in_13);
  and and_9 (and_9_out, P2, in_14);
  and and_10 (and_10_out, P2, in_15);
  and and_11 (and_11_out, P2, in_16);
  and and_12 (and_12_out, P2, in_17);
  and and_13 (and_13_out, P1, in_18);
  and and_14 (and_14_out, P1, in_19);
  and and_15 (and_15_out, P1, in_20);
  and and_16 (and_16_out, P1, in_21);
  and and_17 (and_17_out, P0, in_22);
  and and_18 (and_18_out, P0, in_23);
  and and_19 (and_19_out, P0, in_24);
  and and_20 (and_20_out, P0, in_25);
  or or_1 (D0, and_1_out, and_5_out, and_9_out, and_13_out, and_17_out);
  or or_2 (D1, and_2_out, and_6_out, and_10_out, and_14_out, and_18_out);
  or or_3 (D2, and_3_out, and_7_out, and_11_out, and_15_out, and_19_out);
  or or_4 (D3, and_4_out, and_8_out, and_12_out, and_16_out, and_20_out);
endmodule

module _4_to6_decoder (
  input  B0,
  input  B1,
  input  B2,
  input  B3,
  input  in_5,
  input  edit_enable,
  input  key,
  output out_8,
  output out_9,
  output out_10,
  output out_11,
  output out_12,
  output out_13,
  output out_14,
  output out_15,
  output out_16,
  output out_17,
  output out_18
);

  wire and_1_out, and_3_out, and_5_out, and_7_out, and_10_out, and_11_out, d_ff_1_q, d_ff_2_q, d_ff_3_q,
       d_ff_4_q, not_1_out, not_2_out, not_3_out, not_4_out, not_5_out, not_6_out, not_7_out, not_8_out,
       not_9_out, not_10_out, not_11_out, not_12_out, not_13_out, or_1_out, t_ff_1_q, xnor_1_out;

  T_Flip_Flop t_ff_1 (.clk(edit_enable), .T(edit_enable), .Q(t_ff_1_q), .reset(or_1_out));  // open: Qn, preset, en
  xnor xnor_1 (xnor_1_out, t_ff_1_q, edit_enable);
  or or_1 (or_1_out, in_5, d_ff_4_q);
  D_Flip_Flop #(.trigger("falling")) d_ff_1 (
    .clk(key), .D(d_ff_4_q), .Q(d_ff_1_q), .preset(xnor_1_out), .en(t_ff_1_q));  // open: Qn, reset
  D_Flip_Flop #(.trigger("falling")) d_ff_2 (
    .clk(key), .D(d_ff_1_q), .Q(d_ff_2_q), .en(t_ff_1_q), .reset(xnor_1_out));  // open: Qn, preset
  D_Flip_Flop #(.trigger("falling")) d_ff_3 (
    .clk(key), .D(d_ff_2_q), .Q(d_ff_3_q), .en(t_ff_1_q), .reset(xnor_1_out));  // open: Qn, preset
  D_Flip_Flop #(.trigger("falling")) d_ff_4 (
    .clk(key), .D(d_ff_3_q), .Q(d_ff_4_q), .en(t_ff_1_q), .reset(xnor_1_out));  // open: Qn, preset
  not not_1 (not_1_out, B3);
  and and_1 (and_1_out, not_1_out, B2, not_3_out, not_2_out);
  and and_2 (out_9, d_ff_1_q, and_1_out);
  not not_2 (not_2_out, B0);
  not not_3 (not_3_out, B1);
  not not_4 (not_4_out, B1);
  not not_5 (not_5_out, B3);
  and and_3 (and_3_out, not_5_out, B2, not_4_out, B0);
  and and_4 (out_10, d_ff_1_q, and_3_out);
  not not_6 (not_6_out, B3);
  and and_5 (and_5_out, not_6_out, B1, B2, not_8_out);
  and and_6 (out_11, d_ff_1_q, and_5_out);
  not not_7 (not_7_out, B3);
  not not_8 (not_8_out, B0);
  and and_7 (and_7_out, not_7_out, B2, B1, B1);
  and and_8 (out_12, d_ff_1_q, and_7_out);
  and and_9 (out_13, d_ff_1_q, and_10_out);
  not not_9 (not_9_out, B1);
  not not_10 (not_10_out, B0);
  not not_11 (not_11_out, B2);
  and and_10 (and_10_out, B3, not_11_out, not_9_out, not_10_out);
  not not_12 (not_12_out, B2);
  not not_13 (not_13_out, B1);
  and and_11 (and_11_out, B3, not_12_out, not_13_out, B0);
  and and_12 (out_8, d_ff_2_q, and_1_out);
  and and_13 (out_14, d_ff_2_q, and_3_out);
  and and_14 (out_15, d_ff_2_q, and_5_out);
  and and_15 (out_18, d_ff_2_q, and_10_out);
  and and_16 (out_17, d_ff_2_q, and_7_out);
  and and_17 (out_16, d_ff_2_q, and_11_out);
endmodule

module Buffer (
  input  in_1,
  input  in_2,
  output out_3
);

  wire and_1_out, clock_1_out, d_ff_1_q, d_ff_2_q, d_ff_3_q, d_ff_4_q, d_ff_5_q, not_1_out, not_2_out,
       or_1_out, t_ff_1_q;

  T_Flip_Flop t_ff_1 (.clk(in_1), .T(in_1), .Q(t_ff_1_q));  // open: Qn, preset, reset, en
  D_Flip_Flop d_ff_1 (.Q(d_ff_1_q), .preset(t_ff_1_q), .reset(not_1_out));  // open: clk, D, Qn, en
  not not_1 (not_1_out, t_ff_1_q);
  Clock clock_1 (.out(clock_1_out));
  not not_2 (not_2_out, out_3);
  or or_1 (or_1_out, in_2, out_3);
  and and_1 (and_1_out, d_ff_1_q, clock_1_out);
  D_Flip_Flop d_ff_2 (.clk(and_1_out), .D(not_2_out), .Q(d_ff_2_q), .preset(or_1_out));  // open: Qn, en, reset
  D_Flip_Flop d_ff_3 (.clk(and_1_out), .D(d_ff_2_q), .Q(d_ff_3_q), .reset(or_1_out));  // open: Qn, preset, en
  D_Flip_Flop d_ff_4 (.clk(and_1_out), .D(d_ff_3_q), .Q(d_ff_4_q), .reset(or_1_out));  // open: Qn, preset, en
  D_Flip_Flop d_ff_5 (.clk(and_1_out), .D(d_ff_4_q), .Q(d_ff_5_q), .reset(or_1_out));  // open: Qn, preset, en
  D_Flip_Flop d_ff_6 (.clk(and_1_out), .D(d_ff_5_q), .Q(out_3));  // open: Qn, preset, en, reset
endmodule

module Pattern_lock (
  input  D0,
  input  in_2,
  input  D1,
  input  D2,
  input  D3,
  input  D4,
  input  D5,
  input  D6,
  input  D7,
  input  D8,
  input  D9,
  input  mode,
  input  reset,
  input  Admin,
  input  View,
  input  Edit,
  input  Next,
  output A,
  output B,
  output C,
  output D,
  output E,
  output F,
  output G,
  output Dot,
  output B_2,
  output A_2,
  output F_2,
  output G_2,
  output E_2,
  output D_2,
  output C_2,
  output Dot_2,
  output A_3,
  output B_3,
  output C_3,
  output D_3,
  output E_3,
  output F_3,
  output G_3,
  output Dot_3
);

  wire admin_controller_1_out_17, big_outputgen_1_all_pins_entered_2, big_outputgen_1_ouput,
       big_store_1_admin_2, big_store_1_out_23, big_store_1_out_24, big_store_1_out_25, big_store_1_out_26,
       big_store_1_out_27, big_store_1_out_28, big_store_1_out_29, big_store_1_out_30, big_store_1_out_31,
       big_store_1_out_32, big_store_1_out_33, big_store_1_out_34, big_store_1_out_35, big_store_1_out_36,
       big_store_1_out_37, big_store_1_out_38, big_store_1_out_40, big_store_1_out_41, big_store_1_out_42,
       big_store_1_out_43, big_store_1_s0, big_store_1_s1, big_store_1_s2, big_store_1_s3,
       comparator_1_out_9, comparator_2_out_9, comparator_3_out_9, comparator_4_out_9, comparator_5_out_9,
       cu_1_all_pins_entered, cu_1_c0, cu_1_c1, cu_1_c2, cu_1_c3, cu_1_lock_reset, cu_1_mode_1_2,
       cu_1_p0_enable, cu_1_p1_enable, cu_1_p2_enable, cu_1_p3_enable, cu_1_p4_enable, cu_1_p5_enable,
       cu_1_pass_0_enable, cu_1_pass_1_enable, cu_1_pass_2_enable, cu_1_pass_3_enable, cu_1_pass_4_enable,
       cu_1_s0, cu_1_s1, cu_1_s2, cu_1_s3, decimal_to_excess_3_1_admin_2, decimal_to_excess_3_1_b0,
       decimal_to_excess_3_1_b1, decimal_to_excess_3_1_b2, decimal_to_excess_3_1_b3,
       decimal_to_excess_3_1_constant_enable, decimal_to_excess_3_1_enable, decimal_to_excess_3_1_key,
       decimal_to_excess_3_1_mode_2, decimal_to_excess_3_1_out_30, decimal_to_excess_3_1_out_31,
       decimal_to_excess_3_1_reset_2, decimal_to_excess_3_1_view_2, password_display_1_d0,
       password_display_1_d1, password_display_1_d2, password_display_1_d3;

  Big_store big_store_1 (
    .B0(cu_1_s0), .B1(cu_1_s1), .B2(cu_1_s2), .B3(cu_1_s3), .P5(cu_1_p5_enable), .P4(cu_1_p4_enable),
    .P3(cu_1_p3_enable), .P2(cu_1_p2_enable), .P1(cu_1_p1_enable), .P0(cu_1_p0_enable),
    .in_14(cu_1_pass_4_enable), .in_15(cu_1_pass_3_enable), .in_16(cu_1_pass_2_enable),
    .in_17(cu_1_pass_1_enable), .in_18(cu_1_pass_0_enable), .in_1(cu_1_mode_1_2),
    .enable(decimal_to_excess_3_1_enable), .admin(decimal_to_excess_3_1_admin_2),
    .admin_2(big_store_1_admin_2), .S0(big_store_1_s0), .S1(big_store_1_s1), .S2(big_store_1_s2),
    .S3(big_store_1_s3), .out_23(big_store_1_out_23), .out_24(big_store_1_out_24),
    .out_25(big_store_1_out_25), .out_26(big_store_1_out_26), .out_27(big_store_1_out_27),
    .out_28(big_store_1_out_28), .out_29(big_store_1_out_29), .out_30(big_store_1_out_30),
    .out_31(big_store_1_out_31), .out_32(big_store_1_out_32), .out_33(big_store_1_out_33),
    .out_34(big_store_1_out_34), .out_35(big_store_1_out_35), .out_36(big_store_1_out_36),
    .out_37(big_store_1_out_37), .out_38(big_store_1_out_38), .out_40(big_store_1_out_40),
    .out_41(big_store_1_out_41), .out_42(big_store_1_out_42), .out_43(big_store_1_out_43));
  Decimal_to_Excess_3 decimal_to_excess_3_1 (
    .D0(D0), .D1(D1), .D2(D2), .D3(D3), .D4(D4), .D5(D5), .D6(D6), .D7(D7), .D8(D8), .D9(D9), .mode(mode),
    .reset(reset), .admin(Admin), .View(View), .in_16(Edit), .in_17(Next), .On_Off(in_2),
    .Constant_enable(decimal_to_excess_3_1_constant_enable), .Enable(decimal_to_excess_3_1_enable),
    .Mode_2(decimal_to_excess_3_1_mode_2), .Key(decimal_to_excess_3_1_key),
    .Reset_2(decimal_to_excess_3_1_reset_2), .admin_2(decimal_to_excess_3_1_admin_2),
    .view_2(decimal_to_excess_3_1_view_2), .out_30(decimal_to_excess_3_1_out_30),
    .out_31(decimal_to_excess_3_1_out_31), .B0(decimal_to_excess_3_1_b0), .B1(decimal_to_excess_3_1_b1),
    .B2(decimal_to_excess_3_1_b2), .B3(decimal_to_excess_3_1_b3));  // open: edit
  CU cu_1 (
    .next(decimal_to_excess_3_1_out_31), .Edit_1(decimal_to_excess_3_1_out_30),
    .View(decimal_to_excess_3_1_view_2), .Admin(decimal_to_excess_3_1_admin_2),
    .Reset(decimal_to_excess_3_1_reset_2), .Key(decimal_to_excess_3_1_key),
    .Mode(decimal_to_excess_3_1_mode_2), .Enable(decimal_to_excess_3_1_enable),
    .B0(decimal_to_excess_3_1_b0), .B1(decimal_to_excess_3_1_b1), .B2(decimal_to_excess_3_1_b2),
    .B3(decimal_to_excess_3_1_b3), .S0(cu_1_s0), .S1(cu_1_s1), .S2(cu_1_s2), .S3(cu_1_s3), .C0(cu_1_c0),
    .C1(cu_1_c1), .C2(cu_1_c2), .C3(cu_1_c3), .admin_lock(admin_controller_1_out_17),
    .Mode_1_2(cu_1_mode_1_2), .Lock_reset(cu_1_lock_reset), .P5_enable(cu_1_p5_enable),
    .P4_enable(cu_1_p4_enable), .P3_enable(cu_1_p3_enable), .P2_enable(cu_1_p2_enable),
    .P1_enable(cu_1_p1_enable), .P0_enable(cu_1_p0_enable), .all_pins_entered(cu_1_all_pins_entered),
    .Pass_4_enable(cu_1_pass_4_enable), .Pass_3_enable(cu_1_pass_3_enable),
    .Pass_2_enable(cu_1_pass_2_enable), .Pass_1_enable(cu_1_pass_1_enable), .Pass_0_enable(cu_1_pass_0_enable));  // open: Edit, view_2
  S_S_D s_s_d_1 (
    .z(decimal_to_excess_3_1_b0), .y(decimal_to_excess_3_1_b1), .x(decimal_to_excess_3_1_b2),
    .w(decimal_to_excess_3_1_b3), .enable(decimal_to_excess_3_1_constant_enable), .a(A), .b(B), .c(C), .d(D),
    .e(E), .f(F), .g(G), .DOT(Dot));
  Comparator comparator_1 (
    .C0(cu_1_c0), .C1(cu_1_c1), .C2(cu_1_c2), .C3(cu_1_c3), .S0(big_store_1_s0), .S1(big_store_1_s1),
    .S2(big_store_1_s2), .S3(big_store_1_s3), .out_9(comparator_1_out_9));
  Comparator comparator_2 (
    .C0(cu_1_c0), .C1(cu_1_c1), .C2(cu_1_c2), .C3(cu_1_c3), .S0(big_store_1_out_23), .S1(big_store_1_out_24),
    .S2(big_store_1_out_25), .S3(big_store_1_out_26), .out_9(comparator_2_out_9));
  Comparator comparator_3 (
    .C0(cu_1_c0), .C1(cu_1_c1), .C2(cu_1_c2), .C3(cu_1_c3), .S0(big_store_1_out_27), .S1(big_store_1_out_28),
    .S2(big_store_1_out_29), .S3(big_store_1_out_30), .out_9(comparator_3_out_9));
  Comparator comparator_4 (
    .C0(cu_1_c0), .C1(cu_1_c1), .C2(cu_1_c2), .C3(cu_1_c3), .S0(big_store_1_out_31), .S1(big_store_1_out_32),
    .S2(big_store_1_out_33), .S3(big_store_1_out_34), .out_9(comparator_4_out_9));
  Comparator comparator_5 (
    .C0(cu_1_c0), .C1(cu_1_c1), .C2(cu_1_c2), .C3(cu_1_c3), .S0(big_store_1_out_35), .S1(big_store_1_out_36),
    .S2(big_store_1_out_37), .S3(big_store_1_out_38), .out_9(comparator_5_out_9));
  Admin_controller admin_controller_1 (
    .in_3(cu_1_c0), .in_4(cu_1_c1), .in_5(cu_1_c2), .in_6(cu_1_c3), .in_7(big_store_1_out_40),
    .in_8(big_store_1_out_41), .in_9(big_store_1_out_42), .in_10(big_store_1_out_43),
    .P5_enable(cu_1_p5_enable), .P4_enable(cu_1_p4_enable), .P3_enable(cu_1_p3_enable),
    .P2_enable(cu_1_p2_enable), .P1_enable(cu_1_p1_enable), .P0_enable(cu_1_p0_enable),
    .admin_toggle(big_store_1_admin_2), .reset(cu_1_lock_reset), .out_17(admin_controller_1_out_17));
  Password_Display password_display_1 (
    .in_6(big_store_1_s0), .in_7(big_store_1_s1), .in_8(big_store_1_s2), .in_9(big_store_1_s3),
    .in_10(big_store_1_out_23), .in_11(big_store_1_out_24), .in_12(big_store_1_out_25),
    .in_13(big_store_1_out_26), .in_14(big_store_1_out_27), .in_15(big_store_1_out_28),
    .in_16(big_store_1_out_29), .in_17(big_store_1_out_30), .in_18(big_store_1_out_31),
    .in_19(big_store_1_out_32), .in_20(big_store_1_out_33), .in_21(big_store_1_out_34),
    .in_22(big_store_1_out_35), .in_23(big_store_1_out_36), .in_24(big_store_1_out_37),
    .in_25(big_store_1_out_38), .P4(cu_1_pass_4_enable), .P3(cu_1_pass_3_enable), .P2(cu_1_pass_2_enable),
    .P1(cu_1_pass_1_enable), .P0(cu_1_pass_0_enable), .D0(password_display_1_d0), .D1(password_display_1_d1),
    .D2(password_display_1_d2), .D3(password_display_1_d3));
  big_outputgen big_outputgen_1 (
    .output_1(comparator_1_out_9), .output_2(comparator_2_out_9), .output_3(comparator_3_out_9),
    .output_4(comparator_4_out_9), .output_5(comparator_5_out_9), .p5(cu_1_p5_enable), .P4(cu_1_p4_enable),
    .p3(cu_1_p3_enable), .p2(cu_1_p2_enable), .p1(cu_1_p1_enable), .p0(cu_1_p0_enable),
    .all_pins_entered(cu_1_all_pins_entered), .Mode(cu_1_mode_1_2), .Reset(cu_1_lock_reset),
    .Ouput(big_outputgen_1_ouput), .All_pins_entered_2(big_outputgen_1_all_pins_entered_2));  // open: enter
  SSD_OUT ssd_out_1 (
    .M(cu_1_mode_1_2), .O(big_outputgen_1_ouput), .P5(big_outputgen_1_all_pins_entered_2),
    .admin(admin_controller_1_out_17), .in_1(decimal_to_excess_3_1_constant_enable), .B(B_2), .A(A_2),
    .F(F_2), .G(G_2), .E(E_2), .D(D_2), .C(C_2), .Dot(Dot_2));
  S_S_D s_s_d_2 (
    .z(password_display_1_d0), .y(password_display_1_d1), .x(password_display_1_d2),
    .w(password_display_1_d3), .enable(admin_controller_1_out_17), .a(A_3), .b(B_3), .c(C_3), .d(D_3),
    .e(E_3), .f(F_3), .g(G_3), .DOT(Dot_3));

  // Notes on the sheet:
  //   E M K R Ad V Ed N
endmodule
